# Fritzing sketch Photoresistor (saved by Fritzing 0.9.4)
breadboards: 1

parts:
  Part1 = Arduino Uno (Rev3)
  R1 = PHOTOCELL [package=photocell-kit]
  R2 = Resistor [tolerance=±5% resistance=220 package="0805 [SMD]"]
  LED1 = LED - 5mm [color="Red (633nm)" package="5 mm [THT]"]
  LED2 = LED - 5mm [color="Yellow (585nm)" package="5 mm [THT]"]
  LED3 = LED - 5mm [color="Blue (430nm)" package="5 mm [THT]"]
  R3 = Resistor [tolerance=±5% resistance=220 package="0805 [SMD]"]
  R4 = Resistor [tolerance=±5% resistance=220 package="0805 [SMD]"]
  R5 = Resistor [tolerance=±5% resistance=220 package="0805 [SMD]"]
  LCD1 = LCD screen
  R6 = Resistor [tolerance=±5% resistance=220 package="0805 [SMD]"]
  U1 = POT [package=pot_mammoth]

nets:
  N1: Part1.A5/SCL, R1.P$1
  N2: Part1.D8, LED3.anode
  N3: Part1.D9_PWM, LED2.anode
  N4: Part1.D10_PWM/SS, LED1.anode
  N5: Part1.D11_PWM/MOSI, LCD1.E
  N6: Part1.D12/MISO, LCD1.RS
  GND: Part1.GND, R2.Pin_1, R3.Pin_0, R4.Pin_0, R5.Pin_0, LCD1.VSS, LCD1.R/W, LCD1.LED-, U1.S
  N7: Part1.D2, LCD1.DB7
  N8: Part1.D3_PWM, LCD1.DB6
  N9: Part1.D4, LCD1.DB5
  N10: Part1.D5_PWM, LCD1.DB4
  5V: Part1.5V, LCD1.VDD, R6.Pin_0, U1.E
  N11: R1.P$2, R2.Pin_0
  N12: LED1.cathode, R3.Pin_1
  N13: LED2.cathode, R4.Pin_1
  N14: LED3.cathode, R5.Pin_1
  N15: LCD1.V0, U1.A
  N16: LCD1.LED+, R6.Pin_1

// code stored in the sketch: sketch_nov06a.ino
#include<LiquidCrystal.h>
const int LED1 = 10;
const int LED2 = 9;
const int LED3 = 8;
const int RS = 12;
const int E = 11;
const int D4 = 5;
const int D5 = 4;
const int D6 = 3;
const int D7 = 2;

int analogIn = A5;
int analogValue = 0;

LiquidCrystal lcd(RS,E,D4,D5,D6,D7);

void setup() {
  lcd.begin(16,2);
  lcd.print("Analog Value:");

  pinMode(LED1,OUTPUT);
  pinMode(LED2,OUTPUT);
  pinMode(LED3,OUTPUT);

  pinMode(analogIn, INPUT);
}

void loop() {
  lcd.setCursor(0, 1);
  analogValue = analogRead(analogIn);
  lcd.print(analogValue);
  if(analogValue > 500){
    digitalWrite(LED1,LOW);
    digitalWrite(LED2,LOW);
    digitalWrite(LED3,HIGH);
  }
  else if(analogValue>= 100 && analogValue <= 500){
    digitalWrite(LED1,LOW);
    digitalWrite(LED2,HIGH);
    digitalWrite(LED3,LOW);
  }
  else{
    digitalWrite(LED1,HIGH);
    digitalWrite(LED2,LOW);
    digitalWrite(LED3,LOW);
    
  }
  delay(100);
  
}
